// Logisim project SevenSegmentDecoder.circ as structural Verilog: 2 circuits, main circuit main
module main (
  input  in_1,
  input  in_2,
  input  in_3,
  input  in_4
);

  wire sevenseg_1_sa, sevenseg_1_sb, sevenseg_1_sc, sevenseg_1_sd, sevenseg_1_se, sevenseg_1_sf,
       sevenseg_1_sg;

  SevenSeg sevenseg_1 (
    .a(in_1), .b(in_2), .c(in_3), .d(in_4), .sa(sevenseg_1_sa), .sb(sevenseg_1_sb), .sc(sevenseg_1_sc),
    .sd(sevenseg_1_sd), .se(sevenseg_1_se), .sf(sevenseg_1_sf), .sg(sevenseg_1_sg));
  _7_Segment_Display u_7_segment_display_1 (
    .g(sevenseg_1_sg), .f(sevenseg_1_sf), .a(sevenseg_1_sa), .b(sevenseg_1_sb), .e(sevenseg_1_se),
    .d(sevenseg_1_sd), .c(sevenseg_1_sc));  // open: dp
endmodule

module SevenSeg (
  input  a,
  input  b,
  input  c,
  input  d,
  output sa,
  output sb,
  output sc,
  output sd,
  output se,
  output sf,
  output sg
);

  wire and_1_out, and_2_out, and_3_out, and_4_out, and_5_out, and_6_out, and_7_out, and_8_out, and_9_out,
       and_10_out, and_11_out, and_12_out, and_13_out, not_1_out, not_2_out, not_3_out;

  not not_1 (not_1_out, b);
  not not_2 (not_2_out, c);
  not not_3 (not_3_out, d);
  and and_1 (and_1_out, b, d);
  and and_2 (and_2_out, not_1_out, not_3_out);
  and and_3 (and_3_out, c, d);
  and and_4 (and_4_out, not_2_out, not_3_out);
  or or_1 (sc, b, d, not_2_out);
  and and_5 (and_5_out, c, not_1_out);
  and and_6 (and_6_out, c, not_3_out);
  and and_7 (and_7_out, not_1_out, not_3_out);
  and and_8 (and_8_out, b, d, not_2_out);
  and and_9 (and_9_out, c, not_3_out);
  and and_10 (and_10_out, not_1_out, not_3_out);
  and and_11 (and_11_out, b, not_2_out);
  and and_12 (and_12_out, b, not_3_out);
  and and_13 (and_13_out, not_2_out, not_3_out);
  or or_2 (sa, a, c, and_1_out, and_2_out);
  or or_3 (sb, not_1_out, and_3_out, and_4_out);
  or or_4 (sd, a, and_5_out, and_6_out, and_7_out, and_8_out);
  or or_5 (se, and_9_out, and_10_out);
  or or_6 (sf, a, and_11_out, and_12_out, and_13_out);

  assign sg = 1'b0;
endmodule
